// Logisim project finalproj_v3.circ as structural Verilog: 1 circuit, main circuit main
module main (
  input  true1,
  input  in_2,
  input  in_3,
  input  true,
  input  in_5,
  input  in_6,
  input  true2,
  input  in_8,
  input  in_9,
  input  true3,
  input  in_11,
  input  in_12
);

  wire and_1_out, and_2_out, and_3_out, and_4_out, and_5_out, clock_1_out, d_ff_1_q, d_ff_1_qn, d_ff_2_q,
       d_ff_2_qn, d_ff_3_q, LSB_q, MSB_q, multiplexer_1_out, multiplexer_2_out, multiplexer_3_out,
       multiplexer_4_out, multiplexer_5_out, not_1_out, not_2_out, not_3_out, not_4_out, not_5_out,
       not_6_out, or_1_out, reset_out, stop_out, t_ff_1_q, xor_1_out, xor_2_out, xor_3_out, xor_4_out,
       xor_5_out, xor_6_out;
  wire [2:0] t_ff_2_q, t_ff_3_q, t_ff_4_q;

  Clock clock_1 (.out(clock_1_out));
  D_Flip_Flop d_ff_1 (.D(d_ff_1_qn), .clk(clock_1_out), .Q(d_ff_1_q), .Qn(d_ff_1_qn));  // open: preset, reset
  or or_1 (or_1_out, reset_out, stop_out);
  D_Flip_Flop d_ff_2 (.D(d_ff_2_qn), .clk(d_ff_1_q), .Q(d_ff_2_q), .Qn(d_ff_2_qn));  // open: preset, reset
  T_Flip_Flop t_ff_1 (.T(true1), .clk(or_1_out), .Q(t_ff_1_q));  // open: Qn, reset, preset
  Multiplexer multiplexer_1 (.in0(in_3), .in1(clock_1_out), .out(multiplexer_1_out), .sel(t_ff_1_q));
  Multiplexer multiplexer_2 (.in0(d_ff_1_q), .in1(in_6), .out(multiplexer_2_out), .sel(multiplexer_4_out));
  Multiplexer multiplexer_3 (.in0(d_ff_2_q), .in1(in_11), .out(multiplexer_3_out), .sel(multiplexer_5_out));
  T_Flip_Flop t_ff_2 (.T(true), .clk(multiplexer_1_out), .Q(t_ff_2_q[0]), .reset(reset_out));  // open: Qn, preset
  T_Flip_Flop t_ff_3 (.T(true2), .clk(multiplexer_2_out), .Q(t_ff_3_q[0]), .reset(reset_out));  // open: Qn, preset
  T_Flip_Flop t_ff_4 (.T(true3), .clk(multiplexer_3_out), .Q(t_ff_4_q[0]), .reset(reset_out));  // open: Qn, preset
  T_Flip_Flop t_ff_5 (
    .T(t_ff_2_q[0]), .clk(multiplexer_1_out), .Q(t_ff_2_q[1]), .reset(reset_out));  // open: Qn, preset
  T_Flip_Flop t_ff_6 (
    .T(t_ff_3_q[0]), .clk(multiplexer_2_out), .Q(t_ff_3_q[1]), .reset(reset_out));  // open: Qn, preset
  T_Flip_Flop t_ff_7 (
    .T(t_ff_4_q[0]), .clk(multiplexer_3_out), .Q(t_ff_4_q[1]), .reset(reset_out));  // open: Qn, preset
  and and_1 (and_1_out, t_ff_2_q[0], t_ff_2_q[1]);
  T_Flip_Flop t_ff_8 (.T(and_1_out), .clk(multiplexer_1_out), .Q(t_ff_2_q[2]), .reset(reset_out));  // open: Qn, preset
  and and_2 (and_2_out, t_ff_3_q[0], t_ff_3_q[1]);
  T_Flip_Flop t_ff_9 (.T(and_2_out), .clk(multiplexer_2_out), .Q(t_ff_3_q[2]), .reset(reset_out));  // open: Qn, preset
  and and_3 (and_3_out, t_ff_4_q[0], t_ff_4_q[1]);
  T_Flip_Flop t_ff_10 (.T(and_3_out), .clk(multiplexer_3_out), .Q(t_ff_4_q[2]), .reset(reset_out));  // open: Qn, preset
  Multiplexer multiplexer_4 (.in0(and_4_out), .in1(in_8), .out(multiplexer_4_out), .sel(multiplexer_1_out));
  Multiplexer multiplexer_5 (.in0(in_12), .in1(and_5_out), .out(multiplexer_5_out), .sel(and_4_out));
  D_Flip_Flop LSB (.D(t_ff_2_q[0]), .clk(stop_out), .Q(LSB_q), .preset(reset_out), .reset(reset_out));  // open: Qn
  xor xor_1 (xor_1_out, LSB_q, t_ff_4_q[0]);
  D_Flip_Flop d_ff_3 (
    .D(t_ff_2_q[1]), .clk(stop_out), .Q(d_ff_3_q), .preset(reset_out), .reset(reset_out));  // open: Qn
  xor xor_2 (xor_2_out, LSB_q, t_ff_3_q[0]);
  not not_1 (not_1_out, xor_2_out);
  not not_2 (not_2_out, xor_1_out);
  D_Flip_Flop MSB (.D(t_ff_2_q[2]), .clk(stop_out), .Q(MSB_q), .preset(reset_out), .reset(reset_out));  // open: Qn
  xor xor_3 (xor_3_out, d_ff_3_q, t_ff_3_q[1]);
  not not_3 (not_3_out, xor_3_out);
  xor xor_4 (xor_4_out, d_ff_3_q, t_ff_4_q[1]);
  not not_4 (not_4_out, xor_4_out);
  xor xor_5 (xor_5_out, MSB_q, t_ff_3_q[2]);
  xor xor_6 (xor_6_out, MSB_q, t_ff_4_q[2]);
  not not_5 (not_5_out, xor_6_out);
  Button reset (.out(reset_out));
  Button stop (.out(stop_out));
  Hex_Digit_Display hex_digit_display_1 (.value({in_2, t_ff_2_q}));  // open: dp
  and and_4 (and_4_out, not_1_out, not_3_out, not_6_out);
  not not_6 (not_6_out, xor_5_out);
  and and_5 (and_5_out, not_2_out, not_4_out, not_5_out);
  Hex_Digit_Display hex_digit_display_2 (.value({in_5, t_ff_3_q}));  // open: dp
  Hex_Digit_Display hex_digit_display_3 (.value({in_9, t_ff_4_q}));  // open: dp
endmodule
